# Fritzing sketch room controller (saved by Fritzing 0.9.2b)
stripboards: 4

parts:
  Part1 = Arduino Uno (Rev3)
  T1 = LM35 Temperature Sensor [package="TO92 [THT]"]
  J1 = female pin header, 4 pins [form="♀ (female)"]
  R1 = Photocell (LDR) [package=THT]
  R2 = Resistor [tolerance=±5% resistance=220 package=THT]
  J3 = female pin header, 3 pins [form="♀ (female)"]
  J4 = female pin header, 3 pins [form="♀ (female)"]
  MIC1 = Microphone
  R3 = Resistor [tolerance=±5% resistance=220 package=THT]
  C1 = Ceramic Capacitor [capacitance=100nF package="100 mil [THT, multilayer]"]
  R4 = Resistor [tolerance=±5% resistance=220 package=THT]
  R5 = Resistor [tolerance=±5% resistance=220 package=THT]
  J5 = Piezo Speaker
  R6 = Trimmer Potentiometer [maximum_resistance=10kΩ package=THT]
  LED1 = LED - 5mm [color="Red (633nm)" package="5 mm [THT]"]
  R7 = Resistor [tolerance=±5% resistance=220 package=THT]
  J6 = Infrared Proximity Sensor
  J7 = Infrared Proximity Sensor
  Q1 = PNP-Transistor [package="TO92 [THT]"]
  R8 = Resistor [tolerance=±5% resistance=220 package=THT]
  J8 = female pin header, 2 pins [form="♀ (female)"]
  LED2 = LED - 5mm [color="Infrared (880nm)" package="5 mm [THT]"]
  J9 = Screw terminal - 2 pins [package=THT]
  J10 = female pin header, 2 pins [form="♀ (female)"]
  M1 = DC Motor
  Q2 = NPN-Transistor [package="TO92 [THT]"]
  Q3 = NPN-Transistor [package="TO92 [THT]"]
  Q4 = NPN-Transistor [package="TO92 [THT]"]
  Q5 = NPN-Transistor [package="TO92 [THT]"]
  J11 = female pin header, 2 pins [form="♀ (female)"]
  L1 = Solenoid
  U1 = RELAY [package=relay-g5q]
  Q6 = NPN-Transistor [package="TO92 [THT]"]
  J12 = Screw terminal - 2 pins [package=THT]
  Q7 = NPN-Transistor [package="TO92 [THT]"]
  U2 = RELAY [package=relay-g5q]
  U3 = RELAY [package=relay-g5q]
  J13 = Screw terminal - 2 pins [package=THT]
  Q8 = NPN-Transistor [package="TO92 [THT]"]
  J14 = Screw terminal - 2 pins [package=THT]
  Q9 = NPN-Transistor [package="TO92 [THT]"]
  J15 = female pin header, 2 pins [form="♀ (female)"]
  Q10 = NPN-Transistor [package="TO92 [THT]"]
  J16 = female pin header, 2 pins [form="♀ (female)"]
  U4 = 74HC595 [package="DIP16 [THT]"]
  S1 = Pushbutton [package="[THT]"]
  Q11 = PNP-Transistor [package="TO92 [THT]"]
  R9 = Resistor [tolerance=±5% resistance=220 package=THT]

nets:
  N1: Part1.A0, R6.wiper
  N2: Part1.A1, T1.Vout
  N3: Part1.A2, R4.Pin_1, R5.Pin_0
  N4: Part1.A3, Q1.E, R8.Pin_1
  N5: Part1.A4/SDA, C1.1
  N6: Part1.A5/SCL, R1.pin_1, R2.Pin_0
  N7: Part1.D8, Q7.B
  N8: Part1.D9_PWM, Q8.B
  N9: Part1.D10_PWM/SS, Q9.B
  N10: Part1.D11_PWM/MOSI, Q10.B
  N11: Part1.D12/MISO, J7.Vout
  N12: Part1.D13/SCK, J6.Vout
  GND: Part1.GND, T1.GND, J1.pin2, R2.Pin_1, J3.pin2, J4.pin2, MIC1.pin2, R3.Pin_0, C1.0, R5.Pin_1, J5.pin1, R6.leg2, LED1.cathode, J6.GND, J7.GND, Q1.B, J8.pin1, LED2.cathode, J9.pin2, J10.pin2, M1.pin_2, Q3.C, Q5.E, U1.NO, U2.NO, U3.NO, J15.pin1, J16.pin1, U4.GND, U4.Q7', Q11.B
  N13: Part1.D0/RX, J1.pin4
  N14: Part1.D1/TX, J1.pin3
  N15: Part1.D2, Part1.D4, Q2.B, Q3.B, Q4.B, Q5.B
  N16: Part1.D3_PWM, J8.pin2, LED2.anode
  N17: Part1.D5_PWM, J10.pin1, M1.pin_1
  N18: Part1.D6_PWM, J5.pin2
  N19: Part1.D7, Q6.B
  N20: Part1.3V3, J1.pin1
  VCC: Part1.5V, T1.+Vs, R1.pin_0, J3.pin1, J4.pin1, R3.Pin_1, R4.Pin_0, R6.leg1, R7.Pin_1, J6.Vcc, J7.Vcc, Q1.C, R8.Pin_0, J9.pin1, Q2.E, Q4.C, Q6.C, Q7.C, Q8.C, Q9.E, Q10.E, U4.Q1, U4.VCC, R9.Pin_0
  N21: LED1.anode, R7.Pin_0
  N22: Q2.C, Q3.E, Q4.E, Q5.C, J11.pin1, J11.pin2, L1.pin1, L1.pin2
  N23: U1.COIL2, Q6.E
  N24: U1.MAIN, J12.pin2
  N25: U1.COIL1, J12.pin1
  N26: Q7.E, U2.COIL2
  N27: U2.MAIN, J13.pin2
  N28: U2.COIL1, J13.pin1
  N29: U3.COIL2, Q8.E
  N30: U3.MAIN, J14.pin2
  N31: U3.COIL1, J14.pin1
  N32: Q9.C, J15.pin2
  N33: Q10.C, J16.pin2
  N34: U4.Q2, U4.Q0
  N35: U4.Q3, U4.DS
  N36: U4.Q4, U4.OE
  N37: U4.Q5, U4.ST_CP
  N38: U4.Q6, U4.SH_CP
  N39: U4.Q7, U4.MR
  N40: S1.Pin_1, S1.Pin_2
  N41: S1.Pin_3, S1.Pin_4
  N42: Q11.E, R9.Pin_1

notes:
  ESP8266 module
